// Logisim project 4BitSort.circ as structural Verilog: 3 circuits, main circuit 4bit_sort
module _4bit_sort (
  input  [3:0] in_1,
  input  [3:0] in_2,
  input  [3:0] in_3,
  input  [3:0] in_4,
  output [3:0] out_5,
  output [3:0] out_6,
  output [3:0] out_7,
  output [3:0] out_8
);

  wire comparator_1_gt, comparator_2_gt, comparator_3_gt, comparator_4_gt, comparator_5_gt, comparator_6_gt;
  wire [3:0] n4bit_swap_1_out_4, n4bit_swap_1_out_5, n4bit_swap_2_out_4, n4bit_swap_2_out_5,
       n4bit_swap_3_out_4, n4bit_swap_3_out_5, n4bit_swap_4_out_5, n4bit_swap_5_out_4;

  Comparator #(.width(4), .mode("unsigned")) comparator_1 (.a(in_1), .b(in_2), .gt(comparator_1_gt));  // open: eq, lt
  Comparator #(.width(4), .mode("unsigned")) comparator_2 (.a(in_3), .b(in_4), .gt(comparator_2_gt));  // open: eq, lt
  _4bit_swap u_4bit_swap_1 (
    .in_2(in_1), .in_3(in_2), .in_1(comparator_1_gt), .out_4(n4bit_swap_1_out_4), .out_5(n4bit_swap_1_out_5));
  _4bit_swap u_4bit_swap_2 (
    .in_2(in_3), .in_3(in_4), .in_1(comparator_2_gt), .out_4(n4bit_swap_2_out_4), .out_5(n4bit_swap_2_out_5));
  Comparator #(.width(4), .mode("unsigned")) comparator_3 (
    .a(n4bit_swap_1_out_5), .b(n4bit_swap_2_out_4), .gt(comparator_3_gt));  // open: eq, lt
  _4bit_swap u_4bit_swap_3 (
    .in_2(n4bit_swap_1_out_5), .in_3(n4bit_swap_2_out_4), .in_1(comparator_3_gt), .out_4(n4bit_swap_3_out_4),
    .out_5(n4bit_swap_3_out_5));
  Comparator #(.width(4), .mode("unsigned")) comparator_4 (
    .a(n4bit_swap_1_out_4), .b(n4bit_swap_3_out_4), .gt(comparator_4_gt));  // open: eq, lt
  Comparator #(.width(4), .mode("unsigned")) comparator_5 (
    .a(n4bit_swap_3_out_5), .b(n4bit_swap_2_out_5), .gt(comparator_5_gt));  // open: eq, lt
  _4bit_swap u_4bit_swap_4 (
    .in_2(n4bit_swap_1_out_4), .in_3(n4bit_swap_3_out_4), .in_1(comparator_4_gt), .out_4(out_5),
    .out_5(n4bit_swap_4_out_5));
  _4bit_swap u_4bit_swap_5 (
    .in_2(n4bit_swap_3_out_5), .in_3(n4bit_swap_2_out_5), .in_1(comparator_5_gt), .out_4(n4bit_swap_5_out_4),
    .out_5(out_8));
  Comparator #(.width(4), .mode("unsigned")) comparator_6 (
    .a(n4bit_swap_4_out_5), .b(n4bit_swap_5_out_4), .gt(comparator_6_gt));  // open: eq, lt
  _4bit_swap u_4bit_swap_6 (
    .in_2(n4bit_swap_4_out_5), .in_3(n4bit_swap_5_out_4), .in_1(comparator_6_gt), .out_4(out_6), .out_5(out_7));
endmodule

module _4bit_swap (
  input  in_1,
  input  [3:0] in_2,
  input  [3:0] in_3,
  output [3:0] out_4,
  output [3:0] out_5
);

  _1bit_swap u_1bit_swap_1 (.A(in_2[0]), .B(in_3[0]), .C(in_1), .O1(out_4[0]), .O2(out_5[0]));
  _1bit_swap u_1bit_swap_2 (.A(in_2[1]), .B(in_3[1]), .C(in_1), .O1(out_4[1]), .O2(out_5[1]));
  _1bit_swap u_1bit_swap_3 (.A(in_2[2]), .B(in_3[2]), .C(in_1), .O1(out_4[2]), .O2(out_5[2]));
  _1bit_swap u_1bit_swap_4 (.A(in_2[3]), .B(in_3[3]), .C(in_1), .O1(out_4[3]), .O2(out_5[3]));
endmodule

module _1bit_swap (
  input  A,
  input  B,
  input  C,
  output O1,
  output O2
);

  wire and_1_out, and_2_out, and_3_out, and_4_out, not_1_out, not_2_out;

  not not_1 (not_1_out, C);
  not not_2 (not_2_out, C);
  and and_1 (and_1_out, B, C);
  and and_2 (and_2_out, A, not_1_out);
  and and_3 (and_3_out, B, not_2_out);
  and and_4 (and_4_out, A, C);
  or or_1 (O1, and_1_out, and_2_out);
  or or_2 (O2, and_3_out, and_4_out);
endmodule
