// Logisim project CRC.circ as structural Verilog: 2 circuits, main circuit CRC
module CRC (
  input  [7:0] in_1,
  input  [3:0] in_2,
  output [10:0] out_3
);

  wire clock_1_out, comparator_2_gt, select;
  wire [0:0] multiplexer_1_out;
  wire [2:0] adder_1_out, count, multiplexer_3_out, multiplexer_4_out, next_stage_1_yu, \output ;
  wire [3:0] \input ;

  Multiplexer #(.select(3)) multiplexer_1 (
    .in1(in_1[3]), .in2(in_1[2]), .in3(in_1[1]), .in4(in_1[0]), .out(multiplexer_1_out[0]), .sel(count));  // open: in0, in5, in6, in7, en
  Multiplexer #(.width(4)) multiplexer_2 (
    .in0(in_1[7:4]), .in1({\output , multiplexer_1_out[0]}), .out(\input ), .sel(select));  // open: en
  Comparator #(.width(3), .mode("unsigned")) comparator_1 (.a(count), .b(3'b000), .gt(select));  // open: eq, lt
  Register #(.width(3)) register_1 (.D(multiplexer_3_out), .Q(count), .clk(clock_1_out));  // open: en, clr
  Multiplexer #(.width(3)) multiplexer_3 (
    .in0(count), .in1(adder_1_out), .out(multiplexer_3_out), .sel(comparator_2_gt));  // open: en
  Clock clock_1 (.out(clock_1_out));
  next_stage next_stage_1 (.beichu(\input ), .chushu(in_2), .yu(next_stage_1_yu));  // open: shang
  Multiplexer #(.width(3)) multiplexer_4 (
    .in0(\output ), .in1(next_stage_1_yu), .out(multiplexer_4_out), .sel(comparator_2_gt));  // open: en
  Register #(.width(3)) register_2 (.D(multiplexer_4_out), .Q(\output ), .clk(clock_1_out));  // open: en, clr
  Comparator #(.width(3), .mode("unsigned")) comparator_2 (
    .a(3'b100), .b(count), .gt(comparator_2_gt));  // open: eq, lt
  Adder #(.width(3)) adder_1 (.a(count), .b(3'b001), .out(adder_1_out));  // open: cin, cout
  Multiplexer #(.width(11)) multiplexer_5 (
    .in0({in_1, \output }), .in1({11{1'b0}}), .out(out_3), .sel(comparator_2_gt));  // open: en

  // Other names for the same wires on the sheet: A[7:0] = in_1; B[3:0] = in_2; C[10:0] = out_3
endmodule

module next_stage (
  input  [3:0] beichu,
  input  [3:0] chushu,
  output [2:0] yu,
  output shang
);

  wire [3:0] xor_1_out;

  assign xor_1_out = beichu ^ chushu;  // XOR_Gate xor_1, 4 bits wide
  Multiplexer #(.width(3)) multiplexer_1 (
    .in0(beichu[2:0]), .in1(xor_1_out[2:0]), .out(yu), .sel(beichu[3]));  // open: en

  assign shang = beichu[3];

  // Other names for the same wires on the sheet: A[3:0] = beichu; D = beichu[3]; B[3:0] = chushu; C[2:0] = yu
endmodule
