// Logisim project Mod5.circ as structural Verilog: 1 circuit, main circuit mod5
module mod5 (
  input  In,
  output s0,
  output s1,
  output s2,
  output s3,
  output s4
);

  wire clock_1_out;
  wire [1:1] register_1_q, register_1_q_2;

  Register #(.width(2)) register_1 (
    .D({register_1_q[1], In}), .Q({register_1_q_2[1], register_1_q[1]}), .clk(clock_1_out));  // open: en, clr
  Clock clock_1 (.out(clock_1_out));
  Decoder #(.select(2)) decoder_1 (
    .out0(s1), .out1(s2), .out2(s4), .out3(s3), .sel({register_1_q[1], In}));  // open: en

  assign s0 = 1'b0;
endmodule
