// Logisim project cpu_2.circ as structural Verilog: 13 circuits, main circuit main
module IFU (
  input  clk,
  input  in_2,
  input  [15:0] selPC,
  input  sel_n,
  output [31:0] order,
  output [31:0] pc
);

  wire [31:0] pc_1_next_pc, register_1_q;

  PC pc_1 (.PC(register_1_q), .sel_PC(selPC), .sel_n(sel_n), .next_PC(pc_1_next_pc));
  Register #(.width(32)) register_1 (.D(pc_1_next_pc), .Q(register_1_q), .clk(clk), .clr(in_2));  // open: en
  Adder #(.width(32)) adder_1 (.a(register_1_q), .b(32'h3000), .out(pc));  // open: cin, cout
  IM im_1 (.PC(register_1_q), .\output (order));

  // Other names for the same wires on the sheet: reset = in_2
endmodule

module GRF (
  input  clk,
  input  reset,
  input  WE,
  input  [4:0] A1,
  input  [4:0] A2,
  input  [4:0] A3,
  input  [31:0] WD,
  output [31:0] RD1,
  output [31:0] RD2
);

  wire r1_0, r1_1, r1_2, r1_3, r1_4, r1_5, r1_6, r1_7, r1_8, r1_9, r1_10, r1_11, r1_12, r1_13, r1_14, r1_15,
       r1_16, r1_17, r1_18, r1_19, r1_20, r1_21, r1_22, r1_23, r1_24, r1_25, r1_26, r1_27, r1_28, r1_29,
       r1_30, r1_31, r2_0, r2_1, r2_2, r2_3, r2_4, r2_5, r2_6, r2_7, r2_8, r2_9, r2_10, r2_11, r2_12, r2_13,
       r2_14, r2_15, r2_16, r2_17, r2_18, r2_19, r2_20, r2_21, r2_22, r2_23, r2_24, r2_25, r2_26, r2_27,
       r2_28, r2_29, r2_30, r2_31, r3_0, r3_1, r3_2, r3_3, r3_4, r3_5, r3_6, r3_7, r3_8, r3_9, r3_10, r3_11,
       r3_12, r3_13, r3_14, r3_15, r3_16, r3_17, r3_18, r3_19, r3_20, r3_21, r3_22, r3_23, r3_24, r3_25,
       r3_26, r3_27, r3_28, r3_29, r3_30, r3_31;

  Demultiplexer #(.select(5)) demultiplexer_1 (
    .out0(r1_0), .out1(r1_1), .out2(r1_2), .out3(r1_3), .out4(r1_4), .out5(r1_5), .out6(r1_6), .out7(r1_7),
    .out8(r1_8), .out9(r1_9), .out10(r1_10), .out11(r1_11), .out12(r1_12), .out13(r1_13), .out14(r1_14),
    .out15(r1_15), .out16(r1_16), .out17(r1_17), .out18(r1_18), .out19(r1_19), .out20(r1_20), .out21(r1_21),
    .out22(r1_22), .out23(r1_23), .out24(r1_24), .out25(r1_25), .out26(r1_26), .out27(r1_27), .out28(r1_28),
    .out29(r1_29), .out30(r1_30), .out31(r1_31), .in(1'b1), .sel(A1));  // open: en
  register0 register0_1 (
    .input_data(WD), .clk(clk), .reset(reset), .r1(r1_0), .r2(r2_0), .w(r3_0), .RD1(RD1), .RD2(RD2));
  en_register en_register_1 (
    .input_data(WD), .clk(clk), .reset(reset), .r1(r1_8), .r2(r2_8), .w(r3_8), .RD1(RD1), .RD2(RD2));
  en_register en_register_2 (
    .input_data(WD), .clk(clk), .reset(reset), .r1(r1_16), .r2(r2_16), .w(r3_16), .RD1(RD1), .RD2(RD2));
  en_register en_register_3 (
    .input_data(WD), .clk(clk), .reset(reset), .r1(r1_24), .r2(r2_24), .w(r3_24), .RD1(RD1), .RD2(RD2));
  Demultiplexer #(.select(5)) demultiplexer_2 (
    .out0(r2_0), .out1(r2_1), .out2(r2_2), .out3(r2_3), .out4(r2_4), .out5(r2_5), .out6(r2_6), .out7(r2_7),
    .out8(r2_8), .out9(r2_9), .out10(r2_10), .out11(r2_11), .out12(r2_12), .out13(r2_13), .out14(r2_14),
    .out15(r2_15), .out16(r2_16), .out17(r2_17), .out18(r2_18), .out19(r2_19), .out20(r2_20), .out21(r2_21),
    .out22(r2_22), .out23(r2_23), .out24(r2_24), .out25(r2_25), .out26(r2_26), .out27(r2_27), .out28(r2_28),
    .out29(r2_29), .out30(r2_30), .out31(r2_31), .in(1'b1), .sel(A2));  // open: en
  en_register en_register_4 (
    .input_data(WD), .clk(clk), .reset(reset), .r1(r1_1), .r2(r2_1), .w(r3_1), .RD1(RD1), .RD2(RD2));
  en_register en_register_5 (
    .input_data(WD), .clk(clk), .reset(reset), .r1(r1_9), .r2(r2_9), .w(r3_9), .RD1(RD1), .RD2(RD2));
  en_register en_register_6 (
    .input_data(WD), .clk(clk), .reset(reset), .r1(r1_17), .r2(r2_17), .w(r3_17), .RD1(RD1), .RD2(RD2));
  en_register en_register_7 (
    .input_data(WD), .clk(clk), .reset(reset), .r1(r1_25), .r2(r2_25), .w(r3_25), .RD1(RD1), .RD2(RD2));
  en_register en_register_8 (
    .input_data(WD), .clk(clk), .reset(reset), .r1(r1_26), .r2(r2_26), .w(r3_26), .RD1(RD1), .RD2(RD2));
  en_register en_register_9 (
    .input_data(WD), .clk(clk), .reset(reset), .r1(r1_2), .r2(r2_2), .w(r3_2), .RD1(RD1), .RD2(RD2));
  en_register en_register_10 (
    .input_data(WD), .clk(clk), .reset(reset), .r1(r1_10), .r2(r2_10), .w(r3_10), .RD1(RD1), .RD2(RD2));
  en_register en_register_11 (
    .input_data(WD), .clk(clk), .reset(reset), .r1(r1_18), .r2(r2_18), .w(r3_18), .RD1(RD1), .RD2(RD2));
  Demultiplexer #(.select(5)) demultiplexer_3 (
    .out0(r3_0), .out1(r3_1), .out2(r3_2), .out3(r3_3), .out4(r3_4), .out5(r3_5), .out6(r3_6), .out7(r3_7),
    .out8(r3_8), .out9(r3_9), .out10(r3_10), .out11(r3_11), .out12(r3_12), .out13(r3_13), .out14(r3_14),
    .out15(r3_15), .out16(r3_16), .out17(r3_17), .out18(r3_18), .out19(r3_19), .out20(r3_20), .out21(r3_21),
    .out22(r3_22), .out23(r3_23), .out24(r3_24), .out25(r3_25), .out26(r3_26), .out27(r3_27), .out28(r3_28),
    .out29(r3_29), .out30(r3_30), .out31(r3_31), .in(WE), .sel(A3));  // open: en
  en_register en_register_12 (
    .input_data(WD), .clk(clk), .reset(reset), .r1(r1_3), .r2(r2_3), .w(r3_3), .RD1(RD1), .RD2(RD2));
  en_register en_register_13 (
    .input_data(WD), .clk(clk), .reset(reset), .r1(r1_11), .r2(r2_11), .w(r3_11), .RD1(RD1), .RD2(RD2));
  en_register en_register_14 (
    .input_data(WD), .clk(clk), .reset(reset), .r1(r1_19), .r2(r2_19), .w(r3_19), .RD1(RD1), .RD2(RD2));
  en_register en_register_15 (
    .input_data(WD), .clk(clk), .reset(reset), .r1(r1_27), .r2(r2_27), .w(r3_27), .RD1(RD1), .RD2(RD2));
  en_register en_register_16 (
    .input_data(WD), .clk(clk), .reset(reset), .r1(r1_12), .r2(r2_12), .w(r3_12), .RD1(RD1), .RD2(RD2));
  en_register en_register_17 (
    .input_data(WD), .clk(clk), .reset(reset), .r1(r1_20), .r2(r2_20), .w(r3_20), .RD1(RD1), .RD2(RD2));
  en_register en_register_18 (
    .input_data(WD), .clk(clk), .reset(reset), .r1(r1_28), .r2(r2_28), .w(r3_28), .RD1(RD1), .RD2(RD2));
  en_register en_register_19 (
    .input_data(WD), .clk(clk), .reset(reset), .r1(r1_4), .r2(r2_4), .w(r3_4), .RD1(RD1), .RD2(RD2));
  en_register en_register_20 (
    .input_data(WD), .clk(clk), .reset(reset), .r1(r1_5), .r2(r2_5), .w(r3_5), .RD1(RD1), .RD2(RD2));
  en_register en_register_21 (
    .input_data(WD), .clk(clk), .reset(reset), .r1(r1_13), .r2(r2_13), .w(r3_13), .RD1(RD1), .RD2(RD2));
  en_register en_register_22 (
    .input_data(WD), .clk(clk), .reset(reset), .r1(r1_21), .r2(r2_21), .w(r3_21), .RD1(RD1), .RD2(RD2));
  en_register en_register_23 (
    .input_data(WD), .clk(clk), .reset(reset), .r1(r1_29), .r2(r2_29), .w(r3_29), .RD1(RD1), .RD2(RD2));
  en_register en_register_24 (
    .input_data(WD), .clk(clk), .reset(reset), .r1(r1_6), .r2(r2_6), .w(r3_6), .RD1(RD1), .RD2(RD2));
  en_register en_register_25 (
    .input_data(WD), .clk(clk), .reset(reset), .r1(r1_14), .r2(r2_14), .w(r3_14), .RD1(RD1), .RD2(RD2));
  en_register en_register_26 (
    .input_data(WD), .clk(clk), .reset(reset), .r1(r1_22), .r2(r2_22), .w(r3_22), .RD1(RD1), .RD2(RD2));
  en_register en_register_27 (
    .input_data(WD), .clk(clk), .reset(reset), .r1(r1_30), .r2(r2_30), .w(r3_30), .RD1(RD1), .RD2(RD2));
  en_register en_register_28 (
    .input_data(WD), .clk(clk), .reset(reset), .r1(r1_23), .r2(r2_23), .w(r3_23), .RD1(RD1), .RD2(RD2));
  en_register en_register_29 (
    .input_data(WD), .clk(clk), .reset(reset), .r1(r1_31), .r2(r2_31), .w(r3_31), .RD1(RD1), .RD2(RD2));
  en_register en_register_30 (
    .input_data(WD), .clk(clk), .reset(reset), .r1(r1_7), .r2(r2_7), .w(r3_7), .RD1(RD1), .RD2(RD2));
  en_register en_register_31 (
    .input_data(WD), .clk(clk), .reset(reset), .r1(r1_15), .r2(r2_15), .w(r3_15), .RD1(RD1), .RD2(RD2));
endmodule

module en_register (
  input  [31:0] input_data,
  input  clk,
  input  reset,
  input  r1,
  input  r2,
  input  w,
  output [31:0] RD1,
  output [31:0] RD2
);

  wire [31:0] multiplexer_1_out, register_1_q;

  Multiplexer #(.width(32)) multiplexer_1 (
    .in0(register_1_q), .in1(input_data), .out(multiplexer_1_out), .sel(w));  // open: en
  Register #(.width(32)) register_1 (.D(multiplexer_1_out), .Q(register_1_q), .clk(clk), .clr(reset));  // open: en
  Multiplexer #(.width(32)) multiplexer_2 (.in1(register_1_q), .out(RD1), .sel(r1));  // open: in0, en
  Multiplexer #(.width(32)) multiplexer_3 (.in1(register_1_q), .out(RD2), .sel(r2));  // open: in0, en

  // Other names for the same wires on the sheet: WD[31:0] = input_data
endmodule

module register0 (
  input  [31:0] input_data,
  input  clk,
  input  reset,
  input  r1,
  input  r2,
  input  w,
  output [31:0] RD1,
  output [31:0] RD2
);

  wire [31:0] multiplexer_1_out, register_1_q;

  Multiplexer #(.width(32)) multiplexer_1 (
    .in0(register_1_q), .in1({32{1'b0}}), .out(multiplexer_1_out), .sel(w));  // open: en
  Register #(.width(32)) register_1 (.D(multiplexer_1_out), .Q(register_1_q), .clk(clk), .clr(reset));  // open: en
  Multiplexer #(.width(32)) multiplexer_2 (.in1(register_1_q), .out(RD1), .sel(r1));  // open: in0, en
  Multiplexer #(.width(32)) multiplexer_3 (.in1(register_1_q), .out(RD2), .sel(r2));  // open: in0, en

  // Other names for the same wires on the sheet: WD[31:0] = input_data
endmodule

module ALU (
  input  [31:0] rt,
  input  [2:0] ALUctr,
  input  [31:0] rs,
  input  nPC_sel,
  output [31:0] \output ,
  output equal
);

  wire comparator_1_eq;
  wire [31:0] adder_1_out, or_1_out, subtractor_1_out;

  Adder #(.width(32)) adder_1 (.a(rs), .b(rt), .out(adder_1_out));  // open: cin, cout
  Subtractor #(.width(32)) subtractor_1 (.a(rs), .b(rt), .out(subtractor_1_out));  // open: bin, bout
  assign or_1_out = rs | rt;  // OR_Gate or_1, 32 bits wide
  Comparator #(.width(32), .mode("unsigned")) comparator_1 (.a(rs), .b(rt), .eq(comparator_1_eq));  // open: gt, lt
  Multiplexer multiplexer_1 (.in0(1'b0), .in1(comparator_1_eq), .out(equal), .sel(nPC_sel));  // open: en
  Multiplexer #(.select(3), .width(32)) multiplexer_2 (
    .in1(adder_1_out), .in2(subtractor_1_out), .in4(or_1_out), .out(\output ), .sel(ALUctr));  // open: in0, in3, in5, in6, in7, en
endmodule

module Controller (
  input  [31:0] in_1,
  output RegDst,
  output ALUSrc,
  output MemtoReg,
  output RegWrite,
  output MemWrite,
  output nPC_sel,
  output ExtOp,
  output [2:0] ALUctr,
  output Exthigh
);

  wire add, alu, beq, jal, lui, lw, not_1_out, not_2_out, not_3_out, not_4_out, not_5_out, not_6_out,
       not_7_out, not_8_out, not_9_out, not_10_out, not_11_out, not_12_out, ori, sub, sw;

  not not_1 (not_1_out, in_1[31]);
  not not_2 (not_2_out, in_1[30]);
  or or_1 (RegDst, add, sub);
  not not_3 (not_3_out, in_1[29]);
  or or_2 (ALUSrc, ori, lw, lui, sw);
  not not_4 (not_4_out, in_1[28]);
  buf or_3 (MemtoReg, lw);  // OR_Gate
  not not_5 (not_5_out, in_1[27]);
  not not_6 (not_6_out, in_1[26]);
  or or_4 (RegWrite, ori, add, lui, sub, lw);
  and u_ori (ori, not_1_out, not_2_out, in_1[29], in_1[28], not_5_out, in_1[26]);
  and u_add (alu, not_1_out, not_2_out, not_3_out, not_4_out, not_5_out, not_6_out);
  and u_sub (alu, not_1_out, not_2_out, not_3_out, not_4_out, not_5_out, not_6_out);
  and u_lw (lw, in_1[31], not_2_out, not_3_out, not_4_out, in_1[27], in_1[26]);
  and u_sw (sw, in_1[31], not_2_out, in_1[29], not_4_out, in_1[27], in_1[26]);
  and u_beq (beq, not_1_out, not_2_out, not_3_out, in_1[28], not_5_out, not_6_out);
  and u_lui (lui, not_1_out, not_2_out, in_1[29], in_1[28], in_1[27], in_1[26]);
  and u_jal (jal, not_1_out, not_2_out, not_3_out, not_4_out, in_1[27], in_1[26]);
  buf or_5 (MemWrite, sw);  // OR_Gate
  buf or_6 (nPC_sel, beq);  // OR_Gate
  not not_7 (not_7_out, in_1[5]);
  or or_7 (ExtOp, lw, sw);
  not not_8 (not_8_out, in_1[4]);
  or or_8 (ALUctr[0], add, lw, sw);
  not not_9 (not_9_out, in_1[3]);
  or or_9 (ALUctr[1], sub, beq);
  not not_10 (not_10_out, in_1[2]);
  or or_10 (ALUctr[2], ori, lui);
  not not_11 (not_11_out, in_1[1]);
  not not_12 (not_12_out, in_1[0]);
  buf or_11 (Exthigh, lui);  // OR_Gate
  and and_1 (add, in_1[5], not_8_out, not_9_out, not_10_out, not_11_out, not_12_out, alu);
  and and_2 (sub, in_1[5], not_8_out, not_9_out, not_10_out, in_1[1], not_12_out, alu);

  // Other names for the same wires on the sheet: ALUctr_0 = ALUctr[0]; ALUctr_1 = ALUctr[1]; ALUctr_2 = ALUctr[2];
  //   func0 = in_1[0]; order[31:0] = in_1; func1 = in_1[1]; func2 = in_1[2]; func3 = in_1[3]; func4 = in_1[4];
  //   func5 = in_1[5]; op0 = in_1[26]; op1 = in_1[27]; op2 = in_1[28]; op3 = in_1[29]; op4 = in_1[30]; op5 = in_1[31]
endmodule

module DM (
  input  clk,
  input  MemWrite,
  input  reset,
  input  [31:0] address,
  input  [31:0] data,
  output [31:0] \output 
);

  RAM #(.addrWidth(12), .dataWidth(32), .bus("separate")) ram_1 (
    .addr(address[13:2]), .din(data), .data(\output ), .str(MemWrite), .clk(clk), .clr(reset));  // open: sel, ld
endmodule

module main (
  input  in_1,
  output [31:0] instr,
  output [31:0] out_3,
  output RegWrite,
  output [4:0] RegAddr,
  output [31:0] RegData,
  output MemWrite,
  output [31:0] MemAddr,
  output [31:0] out_9
);

  wire ALUSrc, clk, ExtHigh, ExtOp, MemtoReg, not_1_out, nPC_sel, RegDst, sel_n;
  wire [2:0] ALUcrt;
  wire [4:0] trans_1_rd, trans_1_rs, trans_1_rt;
  wire [15:0] selPC;
  wire [31:0] dm_1_output, ext_1_ext_data, grf_1_rd1, multiplexer_2_out;

  Clock clock_1 (.out(clk));
  IFU ifu_1 (.clk(clk), .in_2(in_1), .selPC(selPC), .sel_n(sel_n), .order(instr), .pc(out_3));
  Trans trans_1 (.\input (instr), .rt(trans_1_rt), .rs(trans_1_rs), .immediate(selPC), .rd(trans_1_rd));
  Controller controller_1 (
    .in_1(instr), .RegDst(RegDst), .ALUSrc(ALUSrc), .MemtoReg(MemtoReg), .RegWrite(RegWrite),
    .MemWrite(MemWrite), .nPC_sel(nPC_sel), .ExtOp(ExtOp), .ALUctr(ALUcrt), .Exthigh(ExtHigh));
  Multiplexer #(.width(5)) multiplexer_1 (.in0(trans_1_rt), .in1(trans_1_rd), .out(RegAddr), .sel(RegDst));  // open: en
  GRF grf_1 (
    .clk(clk), .reset(in_1), .WE(RegWrite), .A1(trans_1_rs), .A2(trans_1_rt), .A3(RegAddr), .WD(RegData),
    .RD1(grf_1_rd1), .RD2(out_9));
  Ext ext_1 (.Ext(ExtOp), .ExtHigh(ExtHigh), .data(selPC), .ext_data(ext_1_ext_data));
  Multiplexer #(.width(32)) multiplexer_2 (
    .in0(out_9), .in1(ext_1_ext_data), .out(multiplexer_2_out), .sel(ALUSrc));  // open: en
  ALU alu_1 (
    .rt(multiplexer_2_out), .ALUctr(ALUcrt), .rs(grf_1_rd1), .\output (MemAddr), .nPC_sel(nPC_sel),
    .equal(sel_n));
  DM dm_1 (.clk(clk), .MemWrite(MemWrite), .reset(in_1), .address(MemAddr), .data(out_9), .\output (dm_1_output));
  not not_1 (not_1_out, MemtoReg);
  Multiplexer #(.width(32)) multiplexer_3 (
    .in0(dm_1_output), .in1(MemAddr), .out(RegData), .sel(not_1_out));  // open: en

  // Other names for the same wires on the sheet: pc[31:0] = out_3; reset = in_1
endmodule

// Thans
module Trans (
  input  [31:0] \input ,
  output [4:0] rd,
  output [4:0] rt,
  output [4:0] rs,
  output [15:0] immediate
);


  assign immediate = \input [15:0];
  assign rd = \input [15:11];
  assign rs = \input [25:21];
  assign rt = \input [20:16];
endmodule

// cal
module cal_address (
  input  [31:0] offset,
  input  [31:0] base,
  output [31:0] address
);

  Adder #(.width(32)) adder_1 (.a(offset), .b(base), .out(address));  // open: cin, cout
endmodule

module Ext (
  input  Ext,
  input  ExtHigh,
  input  [15:0] data,
  output [31:0] ext_data
);

  wire [31:0] bit_extender_1_out, bit_extender_2_out, multiplexer_1_out;

  assign bit_extender_1_out = {{16{1'b0}}, data};  // Bit_Extender bit_extender_1
  assign bit_extender_2_out = {{16{data[15]}}, data};  // Bit_Extender bit_extender_2
  Multiplexer #(.width(32)) multiplexer_1 (
    .in0(bit_extender_1_out), .in1(bit_extender_2_out), .out(multiplexer_1_out), .sel(Ext));  // open: en
  Multiplexer #(.width(32)) multiplexer_2 (
    .in0(multiplexer_1_out), .in1({data, {16{1'b0}}}), .out(ext_data), .sel(ExtHigh));  // open: en
endmodule

module IM (
  input  [31:0] PC,
  output [31:0] \output 
);

  ROM #(.addrWidth(12), .dataWidth(32)) rom_1 (.addr(PC[13:2]), .data(\output ));  // open: sel

  // Notes on the sheet:
  //   contents of rom_1 (hex, n*v repeats v):
  //   341c0000 341d0000 34013456 210820 8c010004 ac010004 3c027878 411822 3c051234 34040005 0 ac85ffff
  //   8c83ffff 10650001 1000000d 34670404 10e3000b 0 3c087777 3508ffff 80022 34001100 e65020 34080000
  //   34090001 340a0001 10a4020 1109fffe 1000ffff
endmodule

module PC (
  input  [31:0] PC,
  input  [15:0] sel_PC,
  input  sel_n,
  output [31:0] next_PC
);

  wire [31:0] adder_1_out, bit_extender_1_out, multiplexer_1_out;

  assign bit_extender_1_out = {{14{sel_PC[15]}}, {sel_PC, 2'b00}};  // Bit_Extender bit_extender_1
  Adder #(.width(32)) adder_1 (.a(PC), .b(bit_extender_1_out), .out(adder_1_out));  // open: cin, cout
  Multiplexer #(.width(32)) multiplexer_1 (
    .in0(PC), .in1(adder_1_out), .out(multiplexer_1_out), .sel(sel_n));  // open: en
  Adder #(.width(32)) adder_2 (.a(multiplexer_1_out), .b(32'h4), .out(next_PC));  // open: cin, cout
endmodule
