// Logisim project fibonacci_1.circ as structural Verilog: 1 circuit, main circuit main
module main (
  input  [2:0] in_1,
  output [3:0] out_2
);

  wire and_1_out, clock_1_out, comparator_1_gt, comparator_2_eq, comparator_3_eq, comparator_4_eq;
  wire [2:0] multiplexer_1_out, register_1_q, subtractor_1_out;
  wire [3:0] adder_1_out, multiplexer_3_out, register_2_q, register_3_q;

  Clock clock_1 (.out(clock_1_out));
  Comparator #(.width(3), .mode("unsigned")) comparator_1 (
    .a(in_1), .b(subtractor_1_out), .gt(comparator_1_gt));  // open: eq, lt
  Multiplexer #(.width(3)) multiplexer_1 (
    .in0(in_1), .in1(subtractor_1_out), .out(multiplexer_1_out), .sel(comparator_1_gt));  // open: en
  Register #(.width(3)) register_1 (.D(multiplexer_1_out), .Q(register_1_q), .clk(and_1_out));  // open: en, clr
  and and_1 (and_1_out, clock_1_out, comparator_4_eq);
  Comparator #(.width(3), .mode("unsigned")) comparator_2 (
    .a(register_1_q), .b(3'b001), .eq(comparator_2_eq));  // open: gt, lt
  Comparator #(.width(3), .mode("unsigned")) comparator_3 (
    .a(subtractor_1_out), .b(3'b000), .eq(comparator_3_eq));  // open: gt, lt
  Subtractor #(.width(3)) subtractor_1 (.a(register_1_q), .b(3'b001), .out(subtractor_1_out));  // open: bin, bout
  Multiplexer #(.width(4)) multiplexer_2 (
    .in0(4'b0000), .in1(register_2_q), .out(out_2), .sel(comparator_2_eq));  // open: en
  Multiplexer #(.width(4)) multiplexer_3 (
    .in0(adder_1_out), .in1(4'b0001), .out(multiplexer_3_out), .sel(comparator_3_eq));  // open: en
  Register #(.width(4)) register_2 (.D(register_3_q), .Q(register_2_q), .clk(and_1_out));  // open: en, clr
  Register #(.width(4)) register_3 (.D(multiplexer_3_out), .Q(register_3_q), .clk(and_1_out));  // open: en, clr
  Adder #(.width(4)) adder_1 (.a(register_2_q), .b(register_3_q), .out(adder_1_out));  // open: cin, cout
  Comparator #(.width(4), .mode("unsigned")) comparator_4 (
    .a(out_2), .b(4'b0000), .eq(comparator_4_eq));  // open: gt, lt
endmodule
