// Logisim project fsm.circ as structural Verilog: 2 circuits, main circuit fsm
module fsm (
  input  in_1,
  input  [1:0] in_2,
  output out_3
);

  wire and_1_out, clock_1_out, not_1_out;
  wire [1:0] multiplexer_1_out, register_1_q, register_2_q, status_trans_1_next_status;

  Register #(.width(2)) register_1 (
    .D(status_trans_1_next_status), .Q(register_1_q), .clk(clock_1_out));  // open: en, clr
  Multiplexer #(.width(2)) multiplexer_1 (
    .in0(register_1_q), .in1(register_2_q), .out(multiplexer_1_out), .sel(not_1_out));  // open: en
  not not_1 (not_1_out, in_1);
  Clock clock_1 (.out(clock_1_out));
  status_trans status_trans_1 (.status(multiplexer_1_out), .ln(in_2), .next_status(status_trans_1_next_status));
  Register #(.width(2)) register_2 (
    .D(status_trans_1_next_status), .Q(register_2_q), .clk(clock_1_out), .clr(and_1_out));  // open: en
  and and_1 (and_1_out, clock_1_out, in_1);
  Comparator #(.width(2), .mode("unsigned")) comparator_1 (
    .a(status_trans_1_next_status), .b(2'b11), .eq(out_3));  // open: gt, lt

  // Other names for the same wires on the sheet: CLR = in_1; ln[1:0] = in_2; Z = out_3
endmodule

module status_trans (
  input  [1:0] status,
  input  [1:0] ln,
  output [1:0] next_status
);

  wire and_1_out, and_2_out, and_3_out, and_4_out, not_1_out, not_2_out, not_3_out, not_4_out, not_5_out,
       not_6_out, not_7_out;

  not not_1 (not_1_out, status[1]);
  not not_2 (not_2_out, ln[0]);
  not not_3 (not_3_out, status[0]);
  not not_4 (not_4_out, ln[0]);
  not not_5 (not_5_out, ln[1]);
  not not_6 (not_6_out, status[0]);
  not not_7 (not_7_out, ln[0]);
  and and_1 (and_1_out, not_1_out, status[0], not_2_out);
  and and_2 (and_2_out, status[1], not_3_out, not_4_out);
  and and_3 (and_3_out, not_5_out, ln[0]);
  and and_4 (and_4_out, status[1], not_6_out, not_7_out);
  or or_1 (next_status[1], and_1_out, and_2_out);
  or or_2 (next_status[0], and_3_out, and_4_out);
endmodule
