// Logisim project fsm_new.circ as structural Verilog: 3 circuits, main circuit fsm
module fsm (
  input  in_1,
  input  [1:0] in_2,
  output out_3
);

  wire clock_1_out, not_1_out;
  wire [1:0] and_1_out, bit_extender_1_out, register_1_q, status_trans_1_out_3;

  not not_1 (not_1_out, in_1);
  assign bit_extender_1_out = {{1{not_1_out}}, not_1_out};  // Bit_Extender bit_extender_1
  status_trans status_trans_1 (.in_1(register_1_q), .in_2(in_2), .out_3(status_trans_1_out_3));
  Clock clock_1 (.out(clock_1_out));
  Register #(.width(2)) register_1 (.D(and_1_out), .Q(register_1_q), .clk(clock_1_out));  // open: en, clr
  assign and_1_out = status_trans_1_out_3 & bit_extender_1_out;  // AND_Gate and_1, 2 bits wide
  \output  output_1 (.in_1(register_1_q), .in_2(in_2), .z(out_3));

  // Other names for the same wires on the sheet: CLR = in_1; ln[1:0] = in_2; Z = out_3
endmodule

module status_trans (
  input  [1:0] in_1,
  input  [1:0] in_2,
  output [1:0] out_3
);

  wire not_1_out, not_2_out;

  not not_1 (not_1_out, in_2[0]);
  not not_2 (not_2_out, in_2[1]);
  and and_1 (out_3[1], in_1[0], not_1_out);
  and and_2 (out_3[0], not_2_out, in_2[0]);
endmodule

module \output  (
  input  [1:0] in_1,
  input  [1:0] in_2,
  output z
);

  wire not_1_out;

  not not_1 (not_1_out, in_2[0]);
  and and_1 (z, in_1[1], not_1_out);
endmodule
