// Logisim project ftoi.circ as structural Verilog: 1 circuit, main circuit ftoi
module ftoi (
  input  [15:0] in_1,
  output [31:0] out_2
);

  wire comparator_1_lt, comparator_2_eq, or_1_out;
  wire [4:0] subtractor_1_out;
  wire [9:0] shifter_1_out;
  wire [21:0] shifter_1_out_2;
  wire [30:0] adder_1_out, bit_extender_2_out, multiplexer_2_out, not_1_out;
  wire [31:0] bit_extender_1_out;

  Comparator #(.width(5), .mode("unsigned")) comparator_1 (
    .a(in_1[14:10]), .b(5'b01111), .lt(comparator_1_lt));  // open: gt, eq
  Comparator #(.width(5), .mode("unsigned")) comparator_2 (
    .a(in_1[14:10]), .b({5{1'b1}}), .eq(comparator_2_eq));  // open: gt, lt
  Multiplexer #(.width(32)) multiplexer_1 (
    .in0({in_1[15], multiplexer_2_out}), .in1({32{1'b0}}), .out(out_2), .sel(or_1_out));  // open: en
  or or_1 (or_1_out, comparator_1_lt, comparator_2_eq);
  Subtractor #(.width(5)) subtractor_1 (.a(in_1[14:10]), .b(5'b01111), .out(subtractor_1_out));  // open: bin, bout
  assign bit_extender_1_out = {{21{1'b0}}, {1'b1, in_1[9:0]}};  // Bit_Extender bit_extender_1
  Shifter #(.width(32)) shifter_1 (
    .in(bit_extender_1_out), .\dist (subtractor_1_out), .out({shifter_1_out_2, shifter_1_out}));
  assign bit_extender_2_out = {{9{1'b0}}, shifter_1_out_2};  // Bit_Extender bit_extender_2
  assign not_1_out = ~bit_extender_2_out;  // NOT_Gate not_1, 31 bits wide
  Multiplexer #(.width(31)) multiplexer_2 (
    .in0(bit_extender_2_out), .in1(adder_1_out), .out(multiplexer_2_out), .sel(in_1[15]));  // open: en
  Adder #(.width(31)) adder_1 (.a(31'h1), .b(not_1_out), .out(adder_1_out));  // open: cin, cout

  // Other names for the same wires on the sheet: M[9:0] = in_1[9:0]; sign = in_1[15]; E[4:0] = in_1[14:10];
  //   output[31:0] = out_2
endmodule
