// Logisim project grf.circ as structural Verilog: 3 circuits, main circuit grf
module grf (
  input  clk,
  input  reset,
  input  WE,
  input  [4:0] A1,
  input  [4:0] A2,
  input  [4:0] A3,
  input  [31:0] WD,
  output [31:0] RD1,
  output [31:0] RD2
);

  wire r1_0, r1_1, r1_2, r1_3, r1_4, r1_5, r1_6, r1_7, r1_8, r1_9, r1_10, r1_11, r1_12, r1_13, r1_14, r1_15,
       r1_16, r1_17, r1_18, r1_19, r1_20, r1_21, r1_22, r1_23, r1_24, r1_25, r1_26, r1_27, r1_28, r1_29,
       r1_30, r1_31, r2_0, r2_1, r2_2, r2_3, r2_4, r2_5, r2_6, r2_7, r2_8, r2_9, r2_10, r2_11, r2_12, r2_13,
       r2_14, r2_15, r2_16, r2_17, r2_18, r2_19, r2_20, r2_21, r2_22, r2_23, r2_24, r2_25, r2_26, r2_27,
       r2_28, r2_29, r2_30, r2_31, r3_0, r3_1, r3_2, r3_3, r3_4, r3_5, r3_6, r3_7, r3_8, r3_9, r3_10, r3_11,
       r3_12, r3_13, r3_14, r3_15, r3_16, r3_17, r3_18, r3_19, r3_20, r3_21, r3_22, r3_23, r3_24, r3_25,
       r3_26, r3_27, r3_28, r3_29, r3_30, r3_31;

  Demultiplexer #(.select(5)) demultiplexer_1 (
    .out0(r1_0), .out1(r1_1), .out2(r1_2), .out3(r1_3), .out4(r1_4), .out5(r1_5), .out6(r1_6), .out7(r1_7),
    .out8(r1_8), .out9(r1_9), .out10(r1_10), .out11(r1_11), .out12(r1_12), .out13(r1_13), .out14(r1_14),
    .out15(r1_15), .out16(r1_16), .out17(r1_17), .out18(r1_18), .out19(r1_19), .out20(r1_20), .out21(r1_21),
    .out22(r1_22), .out23(r1_23), .out24(r1_24), .out25(r1_25), .out26(r1_26), .out27(r1_27), .out28(r1_28),
    .out29(r1_29), .out30(r1_30), .out31(r1_31), .in(1'b1), .sel(A1));  // open: en
  register0 register0_1 (
    .input_data(WD), .clk(clk), .reset(reset), .r1(r1_0), .r2(r2_0), .w(r3_0), .RD1(RD1), .RD2(RD2));
  en_register en_register_1 (
    .input_data(WD), .clk(clk), .reset(reset), .r1(r1_8), .r2(r2_8), .w(r3_8), .RD1(RD1), .RD2(RD2));
  en_register en_register_2 (
    .input_data(WD), .clk(clk), .reset(reset), .r1(r1_16), .r2(r2_16), .w(r3_16), .RD1(RD1), .RD2(RD2));
  en_register en_register_3 (
    .input_data(WD), .clk(clk), .reset(reset), .r1(r1_24), .r2(r2_24), .w(r3_24), .RD1(RD1), .RD2(RD2));
  Demultiplexer #(.select(5)) demultiplexer_2 (
    .out0(r2_0), .out1(r2_1), .out2(r2_2), .out3(r2_3), .out4(r2_4), .out5(r2_5), .out6(r2_6), .out7(r2_7),
    .out8(r2_8), .out9(r2_9), .out10(r2_10), .out11(r2_11), .out12(r2_12), .out13(r2_13), .out14(r2_14),
    .out15(r2_15), .out16(r2_16), .out17(r2_17), .out18(r2_18), .out19(r2_19), .out20(r2_20), .out21(r2_21),
    .out22(r2_22), .out23(r2_23), .out24(r2_24), .out25(r2_25), .out26(r2_26), .out27(r2_27), .out28(r2_28),
    .out29(r2_29), .out30(r2_30), .out31(r2_31), .in(1'b1), .sel(A2));  // open: en
  en_register en_register_4 (
    .input_data(WD), .clk(clk), .reset(reset), .r1(r1_1), .r2(r2_1), .w(r3_1), .RD1(RD1), .RD2(RD2));
  en_register en_register_5 (
    .input_data(WD), .clk(clk), .reset(reset), .r1(r1_9), .r2(r2_9), .w(r3_9), .RD1(RD1), .RD2(RD2));
  en_register en_register_6 (
    .input_data(WD), .clk(clk), .reset(reset), .r1(r1_17), .r2(r2_17), .w(r3_17), .RD1(RD1), .RD2(RD2));
  en_register en_register_7 (
    .input_data(WD), .clk(clk), .reset(reset), .r1(r1_25), .r2(r2_25), .w(r3_25), .RD1(RD1), .RD2(RD2));
  en_register en_register_8 (
    .input_data(WD), .clk(clk), .reset(reset), .r1(r1_26), .r2(r2_26), .w(r3_26), .RD1(RD1), .RD2(RD2));
  en_register en_register_9 (
    .input_data(WD), .clk(clk), .reset(reset), .r1(r1_2), .r2(r2_2), .w(r3_2), .RD1(RD1), .RD2(RD2));
  en_register en_register_10 (
    .input_data(WD), .clk(clk), .reset(reset), .r1(r1_10), .r2(r2_10), .w(r3_10), .RD1(RD1), .RD2(RD2));
  en_register en_register_11 (
    .input_data(WD), .clk(clk), .reset(reset), .r1(r1_18), .r2(r2_18), .w(r3_18), .RD1(RD1), .RD2(RD2));
  Demultiplexer #(.select(5)) demultiplexer_3 (
    .out0(r3_0), .out1(r3_1), .out2(r3_2), .out3(r3_3), .out4(r3_4), .out5(r3_5), .out6(r3_6), .out7(r3_7),
    .out8(r3_8), .out9(r3_9), .out10(r3_10), .out11(r3_11), .out12(r3_12), .out13(r3_13), .out14(r3_14),
    .out15(r3_15), .out16(r3_16), .out17(r3_17), .out18(r3_18), .out19(r3_19), .out20(r3_20), .out21(r3_21),
    .out22(r3_22), .out23(r3_23), .out24(r3_24), .out25(r3_25), .out26(r3_26), .out27(r3_27), .out28(r3_28),
    .out29(r3_29), .out30(r3_30), .out31(r3_31), .in(WE), .sel(A3));  // open: en
  en_register en_register_12 (
    .input_data(WD), .clk(clk), .reset(reset), .r1(r1_3), .r2(r2_3), .w(r3_3), .RD1(RD1), .RD2(RD2));
  en_register en_register_13 (
    .input_data(WD), .clk(clk), .reset(reset), .r1(r1_11), .r2(r2_11), .w(r3_11), .RD1(RD1), .RD2(RD2));
  en_register en_register_14 (
    .input_data(WD), .clk(clk), .reset(reset), .r1(r1_19), .r2(r2_19), .w(r3_19), .RD1(RD1), .RD2(RD2));
  en_register en_register_15 (
    .input_data(WD), .clk(clk), .reset(reset), .r1(r1_27), .r2(r2_27), .w(r3_27), .RD1(RD1), .RD2(RD2));
  en_register en_register_16 (
    .input_data(WD), .clk(clk), .reset(reset), .r1(r1_12), .r2(r2_12), .w(r3_12), .RD1(RD1), .RD2(RD2));
  en_register en_register_17 (
    .input_data(WD), .clk(clk), .reset(reset), .r1(r1_20), .r2(r2_20), .w(r3_20), .RD1(RD1), .RD2(RD2));
  en_register en_register_18 (
    .input_data(WD), .clk(clk), .reset(reset), .r1(r1_28), .r2(r2_28), .w(r3_28), .RD1(RD1), .RD2(RD2));
  en_register en_register_19 (
    .input_data(WD), .clk(clk), .reset(reset), .r1(r1_4), .r2(r2_4), .w(r3_4), .RD1(RD1), .RD2(RD2));
  en_register en_register_20 (
    .input_data(WD), .clk(clk), .reset(reset), .r1(r1_5), .r2(r2_5), .w(r3_5), .RD1(RD1), .RD2(RD2));
  en_register en_register_21 (
    .input_data(WD), .clk(clk), .reset(reset), .r1(r1_13), .r2(r2_13), .w(r3_13), .RD1(RD1), .RD2(RD2));
  en_register en_register_22 (
    .input_data(WD), .clk(clk), .reset(reset), .r1(r1_21), .r2(r2_21), .w(r3_21), .RD1(RD1), .RD2(RD2));
  en_register en_register_23 (
    .input_data(WD), .clk(clk), .reset(reset), .r1(r1_29), .r2(r2_29), .w(r3_29), .RD1(RD1), .RD2(RD2));
  en_register en_register_24 (
    .input_data(WD), .clk(clk), .reset(reset), .r1(r1_6), .r2(r2_6), .w(r3_6), .RD1(RD1), .RD2(RD2));
  en_register en_register_25 (
    .input_data(WD), .clk(clk), .reset(reset), .r1(r1_14), .r2(r2_14), .w(r3_14), .RD1(RD1), .RD2(RD2));
  en_register en_register_26 (
    .input_data(WD), .clk(clk), .reset(reset), .r1(r1_22), .r2(r2_22), .w(r3_22), .RD1(RD1), .RD2(RD2));
  en_register en_register_27 (
    .input_data(WD), .clk(clk), .reset(reset), .r1(r1_30), .r2(r2_30), .w(r3_30), .RD1(RD1), .RD2(RD2));
  en_register en_register_28 (
    .input_data(WD), .clk(clk), .reset(reset), .r1(r1_23), .r2(r2_23), .w(r3_23), .RD1(RD1), .RD2(RD2));
  en_register en_register_29 (
    .input_data(WD), .clk(clk), .reset(reset), .r1(r1_31), .r2(r2_31), .w(r3_31), .RD1(RD1), .RD2(RD2));
  en_register en_register_30 (
    .input_data(WD), .clk(clk), .reset(reset), .r1(r1_7), .r2(r2_7), .w(r3_7), .RD1(RD1), .RD2(RD2));
  en_register en_register_31 (
    .input_data(WD), .clk(clk), .reset(reset), .r1(r1_15), .r2(r2_15), .w(r3_15), .RD1(RD1), .RD2(RD2));
endmodule

module en_register (
  input  [31:0] input_data,
  input  clk,
  input  reset,
  input  r1,
  input  r2,
  input  w,
  output [31:0] RD1,
  output [31:0] RD2
);

  wire [31:0] multiplexer_1_out, register_1_q;

  Multiplexer #(.width(32)) multiplexer_1 (
    .in0(register_1_q), .in1(input_data), .out(multiplexer_1_out), .sel(w));  // open: en
  Register #(.width(32)) register_1 (.D(multiplexer_1_out), .Q(register_1_q), .clk(clk), .clr(reset));  // open: en
  Multiplexer #(.width(32)) multiplexer_2 (.in1(register_1_q), .out(RD1), .sel(r1));  // open: in0, en
  Multiplexer #(.width(32)) multiplexer_3 (.in1(register_1_q), .out(RD2), .sel(r2));  // open: in0, en

  // Other names for the same wires on the sheet: WD[31:0] = input_data
endmodule

module register0 (
  input  [31:0] input_data,
  input  clk,
  input  reset,
  input  r1,
  input  r2,
  input  w,
  output [31:0] RD1,
  output [31:0] RD2
);

  wire [31:0] multiplexer_1_out, register_1_q;

  Multiplexer #(.width(32)) multiplexer_1 (
    .in0(register_1_q), .in1({32{1'b0}}), .out(multiplexer_1_out), .sel(w));  // open: en
  Register #(.width(32)) register_1 (.D(multiplexer_1_out), .Q(register_1_q), .clk(clk), .clr(reset));  // open: en
  Multiplexer #(.width(32)) multiplexer_2 (.in1(register_1_q), .out(RD1), .sel(r1));  // open: in0, en
  Multiplexer #(.width(32)) multiplexer_3 (.in1(register_1_q), .out(RD2), .sel(r2));  // open: in0, en

  // Other names for the same wires on the sheet: WD[31:0] = input_data
endmodule
