// Logisim project navigation.circ as structural Verilog: 3 circuits, main circuit navigation
module navigation (
  input  [1:0] in_1,
  input  in_2,
  input  in_3,
  output out_4,
  output out_5
);

  wire comparator_1_eq, comparator_2_eq, or_1_out, out_put_1_out_4, register_3_q, register_4_q;
  wire [2:0] register_1_q, register_2_q, status_trans_1_out_3;

  Register #(.width(3)) register_1 (.D(register_2_q), .Q(register_1_q), .clk(in_2), .clr(or_1_out));  // open: en
  status_trans status_trans_1 (.in_1(in_1), .in_2(register_2_q), .out_3(status_trans_1_out_3));
  Register #(.width(3)) register_2 (
    .D(status_trans_1_out_3), .Q(register_2_q), .clk(in_2), .clr(or_1_out));  // open: en
  Comparator #(.width(3), .mode("unsigned")) comparator_1 (
    .a(register_1_q), .b(register_2_q), .eq(comparator_1_eq));  // open: gt, lt
  or or_1 (or_1_out, in_3, register_4_q);
  Register #(.width(1)) register_3 (.D(1'b1), .Q(register_3_q), .clk(in_2), .clr(or_1_out));  // open: en
  out_put out_put_1 (.in_1(comparator_1_eq), .in_2(register_2_q), .out_3(out_4), .out_4(out_put_1_out_4));
  Comparator #(.width(1), .mode("unsigned")) comparator_2 (
    .a(register_3_q), .b(1'b1), .eq(comparator_2_eq));  // open: gt, lt
  Register #(.width(1)) register_4 (.D(out_4), .Q(register_4_q), .clk(in_2), .clr(or_1_out));  // open: en
  and and_1 (out_5, out_put_1_out_4, comparator_2_eq);

  // Other names for the same wires on the sheet: arrive = out_4; clk = in_2; dir[1:0] = in_1; hit = out_5;
  //   reset = in_3
endmodule

module status_trans (
  input  [1:0] in_1,
  input  [2:0] in_2,
  output [2:0] out_3
);

  wire and_1_out, and_2_out, and_3_out, and_4_out, and_5_out, and_6_out, and_7_out, and_8_out, and_9_out,
       and_10_out, and_11_out, and_12_out, and_13_out, not_1_out, not_2_out, not_3_out, not_4_out, not_5_out,
       not_6_out, not_7_out, not_8_out, not_9_out, not_10_out, not_11_out, not_12_out, not_13_out,
       not_14_out, not_15_out, not_16_out, not_17_out, not_18_out, not_19_out, not_20_out;

  not not_1 (not_1_out, in_2[0]);
  not not_2 (not_2_out, in_1[1]);
  not not_3 (not_3_out, in_1[1]);
  not not_4 (not_4_out, in_1[0]);
  not not_5 (not_5_out, in_1[1]);
  not not_6 (not_6_out, in_2[1]);
  not not_7 (not_7_out, in_1[1]);
  not not_8 (not_8_out, in_1[1]);
  not not_9 (not_9_out, in_2[0]);
  not not_10 (not_10_out, in_1[1]);
  not not_11 (not_11_out, in_1[0]);
  not not_12 (not_12_out, in_2[0]);
  not not_13 (not_13_out, in_1[0]);
  not not_14 (not_14_out, in_2[2]);
  not not_15 (not_15_out, in_2[1]);
  not not_16 (not_16_out, in_2[0]);
  not not_17 (not_17_out, in_1[1]);
  not not_18 (not_18_out, in_1[0]);
  not not_19 (not_19_out, in_1[0]);
  not not_20 (not_20_out, in_1[0]);
  and and_1 (and_1_out, in_2[1], not_1_out, not_2_out, in_1[0]);
  and and_2 (and_2_out, in_2[1], in_2[0], not_3_out, not_4_out);
  and and_3 (and_3_out, in_2[2], not_5_out);
  and and_4 (and_4_out, not_6_out, in_2[0], not_7_out);
  and and_5 (and_5_out, in_2[0], not_8_out, in_1[0]);
  and and_6 (and_6_out, in_2[1], not_9_out, not_10_out, not_11_out);
  and and_7 (and_7_out, in_2[1], not_12_out, in_1[1], in_1[0]);
  and and_8 (and_8_out, in_2[1], in_2[0], in_1[1], not_13_out);
  and and_9 (and_9_out, in_2[2], in_1[1]);
  and and_10 (and_10_out, not_14_out, not_15_out, not_16_out, not_17_out, not_18_out);
  and and_11 (and_11_out, in_2[0], in_1[0]);
  and and_12 (and_12_out, in_2[1], in_1[1], not_19_out);
  and and_13 (and_13_out, in_2[2], in_1[1], not_20_out);
  or or_1 (out_3[2], and_1_out, and_2_out, and_3_out);
  or or_2 (out_3[1], and_4_out, and_5_out, and_6_out, and_7_out, and_8_out, and_9_out);
  or or_3 (out_3[0], and_10_out, and_11_out, and_12_out, and_13_out);

  // Other names for the same wires on the sheet: dir[1:0] = in_1; next_status[2:0] = out_3; status[2:0] = in_2
endmodule

module out_put (
  input  in_1,
  input  [2:0] in_2,
  output out_3,
  output out_4
);

  Comparator #(.width(3), .mode("unsigned")) comparator_1 (.a(in_2), .b(3'b100), .eq(out_3));  // open: gt, lt

  assign out_4 = in_1;

  // Other names for the same wires on the sheet: arrive = out_3; hit = in_1; is_same = in_1; status[2:0] = in_2
endmodule
