// Logisim project newCRC.circ as structural Verilog: 3 circuits, main circuit CRC
module CRC (
  input  [7:0] in_1,
  input  [3:0] in_2,
  output [10:0] out_3
);

  wire [2:0] n4_crc_1_yu, n4_crc_2_yu, n4_crc_3_yu, n4_crc_4_yu, n4_crc_5_yu, n4_crc_6_yu, n4_crc_7_yu,
       \output ;
  wire [3:0] n8_crc_1_out_5, n8_crc_2_out_5, n8_crc_3_out_5, n8_crc_4_out_5, n8_crc_5_out_5, n8_crc_6_out_5,
       n8_crc_7_out_5, n8_crc_8_out_5;

  _8_CRC u_8_crc_1 (.in_1(in_1), .in_2(in_2), .in_3(3'b000), .in_4(\output ), .out_5(n8_crc_1_out_5));
  _8_CRC u_8_crc_2 (.in_1(in_1), .in_2(in_2), .in_3(3'b001), .in_4(n4_crc_1_yu), .out_5(n8_crc_2_out_5));
  _8_CRC u_8_crc_3 (.in_1(in_1), .in_2(in_2), .in_3(3'b010), .in_4(n4_crc_2_yu), .out_5(n8_crc_3_out_5));
  _8_CRC u_8_crc_4 (.in_1(in_1), .in_2(in_2), .in_3(3'b011), .in_4(n4_crc_3_yu), .out_5(n8_crc_4_out_5));
  _8_CRC u_8_crc_5 (.in_1(in_1), .in_2(in_2), .in_3(3'b100), .in_4(n4_crc_4_yu), .out_5(n8_crc_5_out_5));
  _4_CRC u_4_crc_1 (.beichu(n8_crc_1_out_5), .chushu(in_2), .yu(n4_crc_1_yu));  // open: shang
  _4_CRC u_4_crc_2 (.beichu(n8_crc_2_out_5), .chushu(in_2), .yu(n4_crc_2_yu));  // open: shang
  _4_CRC u_4_crc_3 (.beichu(n8_crc_3_out_5), .chushu(in_2), .yu(n4_crc_3_yu));  // open: shang
  _4_CRC u_4_crc_4 (.beichu(n8_crc_4_out_5), .chushu(in_2), .yu(n4_crc_4_yu));  // open: shang
  _4_CRC u_4_crc_5 (.beichu(n8_crc_5_out_5), .chushu(in_2), .yu(n4_crc_5_yu));  // open: shang
  _8_CRC u_8_crc_6 (.in_1(in_1), .in_2(in_2), .in_3(3'b111), .in_4(n4_crc_7_yu), .out_5(n8_crc_6_out_5));
  _8_CRC u_8_crc_7 (.in_1(in_1), .in_2(in_2), .in_3(3'b111), .in_4(n4_crc_5_yu), .out_5(n8_crc_7_out_5));
  _8_CRC u_8_crc_8 (.in_1(in_1), .in_2(in_2), .in_3(3'b111), .in_4(n4_crc_6_yu), .out_5(n8_crc_8_out_5));
  _4_CRC u_4_crc_6 (.beichu(n8_crc_7_out_5), .chushu(in_2), .yu(n4_crc_6_yu));  // open: shang
  _4_CRC u_4_crc_7 (.beichu(n8_crc_8_out_5), .chushu(in_2), .yu(n4_crc_7_yu));  // open: shang
  _4_CRC u_4_crc_8 (.beichu(n8_crc_6_out_5), .chushu(in_2), .yu(out_3[2:0]));  // open: shang

  assign out_3[10:3] = in_1;

  // Other names for the same wires on the sheet: B[3:0] = in_2; C[10:0] = {in_1, out_3[2:0]}; A[7:0] = in_1
endmodule

module _4_CRC (
  input  [3:0] beichu,
  input  [3:0] chushu,
  output [2:0] yu,
  output shang
);

  wire [3:0] xor_1_out;

  assign xor_1_out = beichu ^ chushu;  // XOR_Gate xor_1, 4 bits wide
  Multiplexer #(.width(3)) multiplexer_1 (
    .in0(beichu[2:0]), .in1(xor_1_out[2:0]), .out(yu), .sel(beichu[3]));  // open: en

  assign shang = beichu[3];

  // Other names for the same wires on the sheet: A[3:0] = beichu; D = beichu[3]; B[3:0] = chushu; C[2:0] = yu
endmodule

module _8_CRC (
  input  [7:0] in_1,
  input  [3:0] in_2,
  input  [2:0] in_3,
  input  [2:0] in_4,
  output [3:0] out_5
);

  wire select;
  wire [0:0] multiplexer_1_out;

  Multiplexer #(.select(3)) multiplexer_1 (
    .in1(in_1[3]), .in2(in_1[2]), .in3(in_1[1]), .in4(in_1[0]), .in7(1'b0), .out(multiplexer_1_out[0]),
    .sel(in_3));  // open: in0, in5, in6, en
  Multiplexer #(.width(4)) multiplexer_2 (
    .in0(in_1[7:4]), .in1({in_4, multiplexer_1_out[0]}), .out(out_5), .sel(select));  // open: en
  Comparator #(.width(3), .mode("unsigned")) comparator_1 (.a(in_3), .b(3'b000), .gt(select));  // open: eq, lt

  // Other names for the same wires on the sheet: A[7:0] = in_1; output[2:0] = in_4; B[3:0] = in_2; count[2:0] = in_3;
  //   input[3:0] = out_5
endmodule
